// Logisim project mips.circ as structural Verilog: 4 circuits, main circuit main
module main (
);

  wire clock_1_out, control_unit_1_alusrc, control_unit_1_regdst, control_unit_1_regwrite,
       demultiplexer_2_out8, demultiplexer_2_out9, demultiplexer_2_out10, Reset_PC_out;
  wire [3:0] control_unit_1_aluop;
  wire [4:0] multiplexer_2_out;
  wire [23:0] adder_1_out, pc_q;
  wire [31:0] alu_1_output, demultiplexer_1_out0, demultiplexer_1_out8, demultiplexer_1_out9,
       demultiplexer_1_out10, multiplexer_1_out, multiplexer_3_out, multiplexer_4_out, ram_1_data,
       sign_extend_1__32bit, t0_q, t1_q, t2_q, zero_q;

  Button Reset_PC (.out(Reset_PC_out));
  Register #(.width(24)) pc (.D(adder_1_out), .Q(pc_q), .clk(clock_1_out), .clr(Reset_PC_out));  // open: en
  Clock clock_1 (.out(clock_1_out));
  Adder #(.width(24)) adder_1 (.a(24'h1), .b(pc_q), .out(adder_1_out));  // open: cin, cout
  RAM #(.addrWidth(24), .dataWidth(32)) ram_1 (
    .addr(pc_q), .data(ram_1_data), .clk(clock_1_out));  // open: sel, ld, clr
  RAM ram_2 ();  // open: addr, data, sel, clk, ld, clr
  Control_Unit control_unit_1 (
    .Instruction(ram_1_data), .RegDst(control_unit_1_regdst), .ALUSrc(control_unit_1_alusrc),
    .RegWrite(control_unit_1_regwrite), .ALUOp(control_unit_1_aluop));  // open: Branch, MemRead, MemtoReg, MemWrite
  Sign_Extend sign_extend_1 (._16bit(ram_1_data[15:0]), ._32bit(sign_extend_1__32bit));
  Register #(.width(32)) zero (
    .D(demultiplexer_1_out0), .Q(zero_q), .clk(clock_1_out), .clr(Reset_PC_out));  // open: en
  Register #(.width(32)) t0 (
    .D(demultiplexer_1_out8), .en(demultiplexer_2_out8), .Q(t0_q), .clk(clock_1_out), .clr(Reset_PC_out));
  Register #(.width(32)) t1 (
    .D(demultiplexer_1_out9), .en(demultiplexer_2_out9), .Q(t1_q), .clk(clock_1_out), .clr(Reset_PC_out));
  Register #(.width(32)) t2 (
    .D(demultiplexer_1_out10), .en(demultiplexer_2_out10), .Q(t2_q), .clk(clock_1_out), .clr(Reset_PC_out));
  Multiplexer #(.select(5), .width(32)) multiplexer_1 (
    .in0(zero_q), .in8(t0_q), .in9(t1_q), .in10(t2_q), .out(multiplexer_1_out), .sel(ram_1_data[25:21]),
    .en(control_unit_1_regwrite));  // open: in1, in2, in3, in4, in5, in6, in7, in11, in12, in13, in14, in15, in16, in17, in18, in19, in20, in21, in22, in23, in24, in25, in26, in27, in28, in29, in30, in31
  Multiplexer #(.width(5)) multiplexer_2 (
    .in0(ram_1_data[15:11]), .in1(ram_1_data[20:16]), .out(multiplexer_2_out), .sel(control_unit_1_alusrc),
    .en(control_unit_1_regwrite));
  Multiplexer #(.select(5), .width(32)) multiplexer_3 (
    .in0(zero_q), .in8(t0_q), .in9(t1_q), .in10(t2_q), .out(multiplexer_3_out), .sel(ram_1_data[20:16]),
    .en(control_unit_1_regwrite));  // open: in1, in2, in3, in4, in5, in6, in7, in11, in12, in13, in14, in15, in16, in17, in18, in19, in20, in21, in22, in23, in24, in25, in26, in27, in28, in29, in30, in31
  Multiplexer #(.width(32)) multiplexer_4 (
    .in0(sign_extend_1__32bit), .in1(multiplexer_3_out), .out(multiplexer_4_out),
    .sel(control_unit_1_regdst), .en(control_unit_1_regwrite));
  ALU alu_1 (.rs(multiplexer_1_out), .rt___I(multiplexer_4_out), .ALU_op(control_unit_1_aluop), .Output(alu_1_output));
  Demultiplexer #(.select(5), .width(32)) demultiplexer_1 (
    .out0(demultiplexer_1_out0), .out8(demultiplexer_1_out8), .out9(demultiplexer_1_out9),
    .out10(demultiplexer_1_out10), .in(alu_1_output), .sel(multiplexer_2_out), .en(control_unit_1_regwrite));  // open: out1, out2, out3, out4, out5, out6, out7, out11, out12, out13, out14, out15, out16, out17, out18, out19, out20, out21, out22, out23, out24, out25, out26, out27, out28, out29, out30, out31
  Demultiplexer #(.select(5)) demultiplexer_2 (
    .out8(demultiplexer_2_out8), .out9(demultiplexer_2_out9), .out10(demultiplexer_2_out10),
    .in(control_unit_1_regwrite), .sel(multiplexer_2_out), .en(control_unit_1_regwrite));  // open: out0, out1, out2, out3, out4, out5, out6, out7, out11, out12, out13, out14, out15, out16, out17, out18, out19, out20, out21, out22, out23, out24, out25, out26, out27, out28, out29, out30, out31

  // Notes on the sheet:
  //   R
  //   I
  //   rs
  //   rt
endmodule

module ALU (
  input  [31:0] rs,
  input  [31:0] rt___I,
  input  [3:0] ALU_op,
  output [31:0] Output
);

  wire [31:0] adder_1_out, and_1_out, nor_1_out, or_1_out, subtractor_1_out;

  assign and_1_out = rs & rt___I;  // AND_Gate and_1, 32 bits wide
  assign or_1_out = rs | rt___I;  // OR_Gate or_1, 32 bits wide
  Adder #(.width(32)) adder_1 (.a(rs), .b(rt___I), .out(adder_1_out));  // open: cin, cout
  assign nor_1_out = ~(rs | rt___I);  // NOR_Gate nor_1, 32 bits wide
  Subtractor #(.width(32)) subtractor_1 (.a(rs), .b(rt___I), .out(subtractor_1_out));  // open: bin, bout
  Multiplexer #(.select(4), .width(32), .enable("false")) multiplexer_1 (
    .in0(and_1_out), .in1(or_1_out), .in2(adder_1_out), .in3(nor_1_out), .in6(subtractor_1_out),
    .out(Output), .sel(ALU_op));  // open: in4, in5, in7, in8, in9, in10, in11, in12, in13, in14, in15

  // Notes on the sheet:
  //   0000 - and
  //   0001 - or
  //   0010 - add
  //   0100 - ??
  //   0101 - ??
  //   0011 - nor?
  //   0110 - sub
  //   0111 - set-on-less-than
endmodule

module Control_Unit (
  input  [31:0] Instruction,
  output RegDst,
  output Branch,
  output MemRead,
  output MemtoReg,
  output MemWrite,
  output ALUSrc,
  output RegWrite,
  output [3:0] ALUOp
);

  wire or_1_out;
  wire [3:0] rom_3_data, rom_4_data;
  wire [6:0] rom_1_data, rom_2_data;

  or or_1 (or_1_out, Instruction[26], Instruction[27], Instruction[28], Instruction[29], Instruction[30], Instruction[31]);
  ROM #(.addrWidth(6), .dataWidth(7)) rom_1 (.addr(Instruction[5:0]), .data(rom_1_data));  // open: sel
  Multiplexer #(.width(7), .enable("false")) multiplexer_1 (
    .in0(rom_1_data), .in1(rom_2_data),
    .out({RegWrite, ALUSrc, MemWrite, MemtoReg, MemRead, Branch, RegDst}), .sel(or_1_out));
  ROM #(.addrWidth(6), .dataWidth(7)) rom_2 (.addr(Instruction[31:26]), .data(rom_2_data));  // open: sel
  ROM #(.addrWidth(6), .dataWidth(4)) rom_3 (.addr(Instruction[5:0]), .data(rom_3_data));  // open: sel
  ROM #(.addrWidth(6), .dataWidth(4)) rom_4 (.addr(Instruction[31:26]), .data(rom_4_data));  // open: sel
  Multiplexer #(.width(4), .enable("false")) multiplexer_2 (
    .in0(rom_3_data), .in1(rom_4_data), .out(ALUOp), .sel(or_1_out));

  // Notes on the sheet:
  //   convert from R function to ALUOp
  //   convert from I function to ALUOp
  //   convert from R function to ALUOp
  //   convert from I opCode to ALUOp
  //   ALUOp
  //   0010 - add
  //   contents of rom_1 (hex, n*v repeats v):
  //   8*0 60 23*0 41 0 41 0 41 41 0 41
  //   contents of rom_2 (hex, n*v repeats v):
  //   8*0 60 0 0 60 60 60
  //   contents of rom_3 (hex, n*v repeats v):
  //   32*0 2 0 6 0 0 1 0 3
  //   contents of rom_4 (hex, n*v repeats v):
  //   8*0 2 0 0 1 0 1
  //   0000 - and
  //   0001 - or
  //   0011 - nor?
  //   0100 - ??
  //   0101 - ??
  //   0110 - sub
  //   0111 - set-on-less-than
  //   sc
  //   RegDst
  //   add R 0x20
  //   addi I 0x8
  //   addiu I 0x9
  //   addu R 0x21
  //   and R 0x24
  //   andi I 0x0c
  //   beq I 0x04
  //   bne I 0x05
  //   j J 0x02
  //   jal J 0x03
  //   jr R 0x03
  //   lbu I 0x24
  //   lhu
  //   ll
  //   lui
  //   lw
  //   nor R 0x27
  //   or R 0x25
  //   ori I 0x0d
  //   slt
  //   slti
  //   sltiu
  //   sltu
  //   sll
  //   srl
  //   sb
  //   sh
  //   sw
  //   sub R 0x22
  //   subu
  //   Branch
  //   MemRead
  //   1             2             4                8                    16                32              64
  //   MemtoReg
  //   MemWrite
  //   1             0             0                0                    0                0              1          = 0x41
  //   0             0             0                0                    0                1              1          = 0x60
  //   0             0             0                0                    0                1              1          = 0x60
  //   1             0             0                0                    0                0              1          = 0x41
  //   1             0             0                0                    0                0              1          = 0x41
  //   0             0             0                0                    0                1              1          = 0x60
  //   0             1             0                0                    0                1              0          = 0x34
  //   0             1             0                0                    0                1              0          = 0x34
  //   0             1             0                0                    0                ?              0          = 0x??
  //   0             1             0                0                    0                ?              0          = 0x??
  //   0            1             0                0                    0                0              0          = 0x02
  //   1             0             0                0                    0                0              1          = 0x41
  //   1             0             0                0                    0                0              1          = 0x41
  //   0             0             0                0                    0                1              1          = 0x60
  //   1             0             0                0                    0                0              1          = 0x41
  //   1             0             0                0                    0                0              1          = 0x41
  //   ALUSrc
  //   RegWrite
endmodule

module Sign_Extend (
  input  [15:0] _16bit,
  output [31:0] _32bit
);


  assign _32bit = {{17{_16bit[15]}}, _16bit[14:0]};
endmodule
